# Fritzing sketch Programming Sketch (saved by Fritzing 0.9.2b)
breadboards: 1

parts:
  ESP8266-1 = ESP8266-12 [part_number=ESP8266-12]
  R1 = Resistor [tolerance=±5% resistance=10k package=THT]
  R2 = Resistor [tolerance=±5% resistance=10k package=THT]
  R3 = Resistor [tolerance=±5% resistance=10k package=THT]
  R4 = Resistor [tolerance=±5% resistance=10k package=THT]
  R5 = Resistor [tolerance=±5% resistance=10k package=THT]
  FTDI = FTDI Basic Programmer
  Program = Pushbutton [package="[THT]"]
  Reset = Pushbutton [package="[THT]"]

nets (from the schematic view):
  N1: ESP8266-1.REST, R4.Pin_0, Reset.Pin_1, Reset.Pin_2
  N2: ESP8266-1.CH_PD, R5.Pin_0
  N3: ESP8266-1.VCC, R2.Pin_1, R3.Pin_1, R4.Pin_1, R5.Pin_1, FTDI.POWER
  N4: ESP8266-1.TXD, FTDI.RXI
  N5: ESP8266-1.RXD, FTDI.TXO
  N6: ESP8266-1.GPIO0, R3.Pin_0, Program.Pin_3, Program.Pin_4
  N7: ESP8266-1.GPIO2, R2.Pin_0
  N8: ESP8266-1.GPIO15, R1.Pin_0
  GND: ESP8266-1.GND, R1.Pin_1, FTDI.GND, Program.Pin_1, Program.Pin_2, Reset.Pin_3, Reset.Pin_4

notes:
  CTS and DTR are not used
