# Fritzing sketch TrainDevice (saved by Fritzing 0.9.2b)

parts:
  ESP8266-1 = ESP8266-12 [part_number=ESP8266-12]
  Puerto_de_comunicación = Header 4 [package=molex-1x4_lock]
  J1 = Power Jack [package=power_jack_combo]
  M1 = DC Motor
  C1 = Electrolytic Capacitor [capacitance=1μF package="0405 [SMD, electrolytic]"]
  IC1 = Voltage Regulator [part_number=662K package=to-92]
  U1 = Voltage Regulator [part_number=78L05 package=to-220-alt]
  IC2 = L293D [package=THT]
  D1 = Diode [package=diode-hv]
  D3 = Diode [package=diode-hv]
  D4 = Diode [package=diode-hv]
  D2 = Diode [package=diode-hv]

nets:
  N1: ESP8266-1.CH_PD, ESP8266-1.VCC, Puerto_de_comunicación.1, IC1.OUT
  N2: ESP8266-1.GPIO16, IC2.In_1
  N3: ESP8266-1.GPIO14, IC2.In_2
  N4: ESP8266-1.TXD, Puerto_de_comunicación.2
  N5: ESP8266-1.RXD, Puerto_de_comunicación.3
  GND: ESP8266-1.GND, Puerto_de_comunicación.4, C1.-, IC1.GND, U1.GND, IC2.0V, D1.A, D3.A
  N6: J1.GND, D3.C, D4.A
  N7: J1.PWR, D1.C, D2.A
  N8: M1.pin_1, IC2.Out_2_(_Controlled_by_Enable_1_)
  N9: M1.pin_2, IC2.Out_1_(_Controlled_by_Enable_1_)
  N10: C1.+, U1.IN, IC2.+Vmotor, D4.C, D2.C
  N11: IC1.IN, U1.OUT, IC2.Enable_1
